# Fritzing sketch CPLD_hexDisplay (saved by Fritzing 0.9.3b)
breadboards: 1

parts:
  7_Segment1 = 7 Segment Display
  R1 = Resistor [tolerance=±5% resistance=680 package="0805 [SMD]"]
  R2 = Resistor [tolerance=±5% resistance=680 package="0805 [SMD]"]
  R3 = Resistor [tolerance=±5% resistance=680 package="0805 [SMD]"]
  R4 = Resistor [tolerance=±5% resistance=680 package="0805 [SMD]"]
  R5 = Resistor [tolerance=±5% resistance=680 package="0805 [SMD]"]
  R6 = Resistor [tolerance=±5% resistance=680 package="0805 [SMD]"]
  R7 = Resistor [tolerance=±5% resistance=680 package="0805 [SMD]"]
  Part1 = Arduino Uno (Rev3) - ICSP  # not connected

nets:
  N1: 7_Segment1.Segment_A#1, R4.Pin_0
  N2: 7_Segment1.Segment_F, R5.Pin_0
  N3: 7_Segment1.Segment_E, R6.Pin_0
  N4: 7_Segment1.Segment_D, R7.Pin_0
  N5: 7_Segment1.Segment_C, R1.Pin_0
  N6: 7_Segment1.Segment_B, R2.Pin_0
  N7: 7_Segment1.Segment_A#10, R3.Pin_0
